// Logisim project Guess the Number Xtreme.circ as structural Verilog
module somador4b (
  input  [3:0] in_1,
  input  [3:0] in_2,
  output [4:0] out_3
);

  Adder #(.width(4)) adder_1 (.a(in_1), .b(in_2), .out(out_3[3:0]), .cout(out_3[4]));  // open: cin
endmodule

module comparador5b (
  input  [4:0] in_1,
  input  [4:0] in_2,
  output out_3,
  output out_4,
  output out_5
);

  wire and_1_out, and_2_out, and_3_out, and_4_out, and_5_out, and_6_out, and_7_out, and_8_out,
       comp1b_1_out_3, comp1b_1_out_4, comp1b_1_out_5, comp1b_2_out_3, comp1b_2_out_4, comp1b_2_out_5,
       comp1b_3_out_3, comp1b_3_out_4, comp1b_3_out_5, comp1b_4_out_3, comp1b_4_out_4, comp1b_4_out_5,
       comp1b_5_out_3, comp1b_5_out_4, comp1b_5_out_5;

  comp1b comp1b_1 (.a(in_1[0]), .b(in_2[0]), .out_3(comp1b_1_out_3), .out_4(comp1b_1_out_4), .out_5(comp1b_1_out_5));
  comp1b comp1b_2 (.a(in_1[1]), .b(in_2[1]), .out_3(comp1b_2_out_3), .out_4(comp1b_2_out_4), .out_5(comp1b_2_out_5));
  comp1b comp1b_3 (.a(in_1[4]), .b(in_2[4]), .out_3(comp1b_3_out_3), .out_4(comp1b_3_out_4), .out_5(comp1b_3_out_5));
  comp1b comp1b_4 (.a(in_1[3]), .b(in_2[3]), .out_3(comp1b_4_out_3), .out_4(comp1b_4_out_4), .out_5(comp1b_4_out_5));
  comp1b comp1b_5 (.a(in_1[2]), .b(in_2[2]), .out_3(comp1b_5_out_3), .out_4(comp1b_5_out_4), .out_5(comp1b_5_out_5));
  and and_1 (and_1_out, comp1b_3_out_3, comp1b_4_out_4);
  and and_2 (and_2_out, comp1b_3_out_3, comp1b_4_out_3, comp1b_5_out_4);
  and and_3 (and_3_out, comp1b_3_out_3, comp1b_4_out_3, comp1b_5_out_3, comp1b_2_out_4);
  and and_4 (and_4_out, comp1b_3_out_3, comp1b_4_out_3, comp1b_5_out_3, comp1b_2_out_3, comp1b_1_out_4);
  and and_5 (and_5_out, comp1b_3_out_3, comp1b_4_out_5);
  and and_6 (and_6_out, comp1b_3_out_3, comp1b_4_out_3, comp1b_5_out_5);
  and and_7 (and_7_out, comp1b_3_out_3, comp1b_4_out_3, comp1b_5_out_3, comp1b_2_out_5);
  and and_8 (and_8_out, comp1b_3_out_3, comp1b_4_out_3, comp1b_5_out_3, comp1b_2_out_3, comp1b_1_out_5);
  and and_9 (out_3, comp1b_3_out_3, comp1b_4_out_3, comp1b_5_out_3, comp1b_2_out_3, comp1b_1_out_3);
  or or_1 (out_4, comp1b_3_out_4, and_1_out, and_4_out, and_2_out, and_3_out);
  or or_2 (out_5, comp1b_3_out_5, and_5_out, and_8_out, and_6_out, and_7_out);
endmodule

module comparador4b (
  input  [3:0] in_1,
  input  [3:0] in_2,
  output out_3,
  output out_4,
  output out_5
);

  wire and_1_out, and_2_out, and_3_out, and_4_out, and_5_out, and_6_out, comp1b_1_out_3, comp1b_1_out_4,
       comp1b_1_out_5, comp1b_2_out_3, comp1b_2_out_4, comp1b_2_out_5, comp1b_3_out_3, comp1b_3_out_4,
       comp1b_3_out_5, comp1b_4_out_3, comp1b_4_out_4, comp1b_4_out_5;

  comp1b comp1b_1 (.a(in_1[3]), .b(in_2[3]), .out_3(comp1b_1_out_3), .out_4(comp1b_1_out_4), .out_5(comp1b_1_out_5));
  comp1b comp1b_2 (.a(in_1[2]), .b(in_2[2]), .out_3(comp1b_2_out_3), .out_4(comp1b_2_out_4), .out_5(comp1b_2_out_5));
  comp1b comp1b_3 (.a(in_1[1]), .b(in_2[1]), .out_3(comp1b_3_out_3), .out_4(comp1b_3_out_4), .out_5(comp1b_3_out_5));
  comp1b comp1b_4 (.a(in_1[0]), .b(in_2[0]), .out_3(comp1b_4_out_3), .out_4(comp1b_4_out_4), .out_5(comp1b_4_out_5));
  and and_1 (and_1_out, comp1b_1_out_3, comp1b_2_out_4);
  and and_2 (and_2_out, comp1b_2_out_3, comp1b_1_out_3, comp1b_3_out_4);
  and and_3 (and_3_out, comp1b_1_out_3, comp1b_3_out_3, comp1b_4_out_4, comp1b_2_out_3);
  and and_4 (and_4_out, comp1b_1_out_3, comp1b_2_out_5);
  and and_5 (and_5_out, comp1b_1_out_3, comp1b_2_out_3, comp1b_3_out_5);
  and and_6 (and_6_out, comp1b_1_out_3, comp1b_2_out_3, comp1b_3_out_3, comp1b_4_out_5);
  and and_7 (out_3, comp1b_2_out_3, comp1b_1_out_3, comp1b_3_out_3, comp1b_4_out_3);
  or or_1 (out_4, comp1b_1_out_4, and_1_out, and_2_out, and_3_out);
  or or_2 (out_5, comp1b_1_out_5, and_4_out, and_5_out, and_6_out);
endmodule

module diff5b (
  input  [4:0] in_1,
  input  [4:0] in_2,
  output [4:0] out_3
);

  wire subtrator1b_1_bout, subtrator1b_2_bout, subtrator1b_3_bout, subtrator1b_4_bout;

  subtrator1b subtrator1b_1 (.a(in_1[0]), .b(in_2[0]), .bin(1'b0), .diff(out_3[0]), .bout(subtrator1b_1_bout));
  subtrator1b subtrator1b_2 (
    .a(in_1[1]), .b(in_2[1]), .bin(subtrator1b_1_bout), .diff(out_3[1]), .bout(subtrator1b_2_bout));
  subtrator1b subtrator1b_3 (
    .a(in_1[2]), .b(in_2[2]), .bin(subtrator1b_2_bout), .diff(out_3[2]), .bout(subtrator1b_3_bout));
  subtrator1b subtrator1b_4 (
    .a(in_1[3]), .b(in_2[3]), .bin(subtrator1b_3_bout), .diff(out_3[3]), .bout(subtrator1b_4_bout));
  subtrator1b subtrator1b_5 (.a(in_1[4]), .b(in_2[4]), .bin(subtrator1b_4_bout), .diff(out_3[4]));  // open: bout
endmodule

module subtrator1b (
  input  a,
  input  b,
  input  bin,
  output diff,
  output bout
);

  wire and_1_out, and_2_out, and_3_out, xor_1_out;

  xor xor_1 (xor_1_out, a, b);
  and and_1 (and_1_out, b, bin);
  and and_2 (and_2_out, ~a, bin);  // AND_Gate
  and and_3 (and_3_out, ~a, b);  // AND_Gate
  xor xor_2 (diff, xor_1_out, bin);
  or or_1 (bout, and_1_out, and_2_out, and_3_out);
endmodule

// cores
module cores5b (
  input  [4:0] num,
  output [7:0] vermelho,
  output [7:0] azul
);

  assign vermelho = ~{num, {3{num[4]}}};  // NOT_Gate not_1, 8 bits wide

  assign azul = {num, {3{num[4]}}};
endmodule

module mux1b (
  input  a,
  input  b,
  input  c,
  output x
);

  wire and_1_out, and_2_out, not_1_out;

  not not_1 (not_1_out, a);
  and and_1 (and_1_out, not_1_out, b);
  and and_2 (and_2_out, a, c);
  or or_1 (x, and_1_out, and_2_out);
endmodule

module diffmux5b (
  input  [4:0] x,
  input  [4:0] y,
  output [4:0] out_3
);

  wire comparador5b_1_out_3;
  wire [4:0] mux5b_1_out_4, mux5b_2_out_4;

  comparador5b comparador5b_1 (.in_1(x), .in_2(y), .out_3(comparador5b_1_out_3));  // open: out_4, out_5
  mux5b mux5b_1 (.a(y), .b(x), .chave(comparador5b_1_out_3), .out_4(mux5b_1_out_4));
  diff5b diff5b_1 (.in_1(mux5b_1_out_4), .in_2(mux5b_2_out_4), .out_3(out_3));
  mux5b mux5b_2 (.a(x), .b(y), .chave(comparador5b_1_out_3), .out_4(mux5b_2_out_4));
endmodule

module mux5b (
  input  [4:0] a,
  input  [4:0] b,
  input  chave,
  output [4:0] out_4
);

  mux1b mux1b_1 (.a(chave), .b(a[4]), .c(b[4]), .x(out_4[4]));
  mux1b mux1b_2 (.a(chave), .b(a[3]), .c(b[3]), .x(out_4[3]));
  mux1b mux1b_3 (.a(chave), .b(a[2]), .c(b[2]), .x(out_4[2]));
  mux1b mux1b_4 (.a(chave), .b(a[1]), .c(b[1]), .x(out_4[1]));
  mux1b mux1b_5 (.a(chave), .b(a[0]), .c(b[0]), .x(out_4[0]));
endmodule

module comp1b (
  input  a,
  input  b,
  output out_3,
  output out_4,
  output out_5
);

  wire and_1_out, and_2_out, not_1_out, not_2_out, not_3_out, not_4_out;

  not not_1 (not_1_out, a);
  not not_2 (not_2_out, b);
  not not_3 (not_3_out, b);
  not not_4 (not_4_out, a);
  and and_1 (and_1_out, not_1_out, not_2_out);
  and and_2 (and_2_out, a, b);
  and and_3 (out_4, a, not_3_out);
  and and_4 (out_5, not_4_out, b);
  or or_1 (out_3, and_1_out, and_2_out);
endmodule

module Estado_de_Jogo (
  input  Iniciar,
  input  Game_Reset,
  output Rodando,
  output End_Config
);

  S_R_Flip_Flop s_r_ff_1 (.Q(Rodando), .Qn(End_Config), .preset(Iniciar), .reset(Game_Reset));  // open: S, clk, R

  // Notes on the sheet:
  //   Circuito de estado de jogo
endmodule

module GTN_X (
  input  Confirmar,
  input  Novo,
  input  [3:0] x,
  input  [3:0] y,
  output [7:0] VERMELHO,
  output [7:0] AZUL,
  output X_CERTO,
  output Y_CERTO,
  output SOMA_CERTA,
  output [3:0] X_R,
  output [3:0] Y_R
);

  wire comp4b_2_out_3, comp4b_out_3, comp5b_out_3;
  wire [4:0] diffmux_out_3, soma4b_2_out_3, soma4b_out_3;
  wire [7:0] bit_extender_1_out, cores5b_1_azul, cores5b_1_vermelho;

  Random random_1 (.clk(Novo), .out({Y_R, X_R}));  // open: next, clr
  assign bit_extender_1_out = {{7{Confirmar}}, Confirmar};  // Bit_Extender bit_extender_1
  somador4b soma4b (.in_1(Y_R), .in_2(X_R), .out_3(soma4b_out_3));
  somador4b soma4b_2 (.in_1(x), .in_2(y), .out_3(soma4b_2_out_3));
  and and_1 (X_CERTO, Confirmar, comp4b_out_3);
  comparador4b comp4b (.in_1(X_R), .in_2(x), .out_3(comp4b_out_3));  // open: out_4, out_5
  and and_2 (Y_CERTO, Confirmar, comp4b_2_out_3);
  comparador4b comp4b_2 (.in_1(Y_R), .in_2(y), .out_3(comp4b_2_out_3));  // open: out_4, out_5
  and and_3 (SOMA_CERTA, Confirmar, comp5b_out_3);
  comparador5b comp5b (.in_1(soma4b_out_3), .in_2(soma4b_2_out_3), .out_3(comp5b_out_3));  // open: out_4, out_5
  assign VERMELHO = bit_extender_1_out & cores5b_1_vermelho;  // AND_Gate and_4, 8 bits wide
  diffmux5b diffmux (.x(soma4b_out_3), .y(soma4b_2_out_3), .out_3(diffmux_out_3));
  assign AZUL = cores5b_1_azul & bit_extender_1_out;  // AND_Gate and_5, 8 bits wide
  cores5b cores5b_1 (.num(diffmux_out_3), .vermelho(cores5b_1_vermelho), .azul(cores5b_1_azul));
endmodule

module teste_GTN_X (
  input  [3:0] in_1,
  input  [3:0] in_2,
  output X,
  output Y,
  output Soma
);

  wire Confirmar_out, Sortear_out;
  wire [7:0] rgbled_1_p1, rgbled_1_p2;

  Button Confirmar (.out(Confirmar_out));
  Button Sortear (.out(Sortear_out));
  // RGBLed #(.multibit("true")) rgbled_1: pin names not known; wires that end beside it: rgbled_1_p1, rgbled_1_p2
  GTN_X gtn_x_1 (
    .Confirmar(Confirmar_out), .Novo(Sortear_out), .x(in_1), .y(in_2), .X_CERTO(X), .Y_CERTO(Y),
    .SOMA_CERTA(Soma), .VERMELHO(rgbled_1_p1), .AZUL(rgbled_1_p2));  // open: X_R, Y_R
endmodule

module Controle_de_turnos (
  input  Iniciar_jogo,
  input  \Avançar_B ,
  input  \Avançar_A ,
  input  Resetar_jogo,
  output A_jogando,
  output B_jogando
);

  wire or_1_out;

  or or_1 (or_1_out, \Avançar_B , \Avançar_A );
  S_R_Flip_Flop s_r_ff_1 (
    .S(\Avançar_B ), .clk(or_1_out), .R(\Avançar_A ), .Q(A_jogando), .Qn(B_jogando), .preset(Iniciar_jogo),
    .reset(Resetar_jogo));
  Estado_de_Jogo Estado_de_jogo (.Iniciar(Iniciar_jogo), .Game_Reset(Resetar_jogo));  // open: Rodando, End_Config

  // Notes on the sheet:
  //   Circuito de Controle de turnos
endmodule

module \Cronômetro_B  (
  input  in_1,
  input  in_2,
  input  m1b,
  input  m0b,
  input  s1b,
  input  s0b,
  input  CLK,
  input  B_jogando,
  output [3:0] M1B_2,
  output [3:0] M0B_2,
  output [3:0] S1B_2,
  output [3:0] S0B_2
);

  wire and_1_out, Dezena_de_segundo_carry, multiplexer_1_out, multiplexer_2_out, multiplexer_3_out,
       multiplexer_4_out, Unidade_de_minuto_carry, Unidade_de_segundo_carry;

  Counter #(.width(4), .max('h5)) Dezena_de_minuto (
    .count(in_2), .Q(M1B_2), .clk(multiplexer_1_out));  // open: load, D, carry, clr, preset, down
  Multiplexer #(.enable("false")) multiplexer_1 (
    .in0(Unidade_de_minuto_carry), .in1(m1b), .out(multiplexer_1_out), .sel(in_2));
  Counter #(.width(4), .max('h9)) Unidade_de_minuto (
    .count(in_2), .Q(M0B_2), .carry(Unidade_de_minuto_carry), .clk(multiplexer_2_out));  // open: load, D, clr, preset, down
  Multiplexer #(.enable("false")) multiplexer_2 (
    .in0(Dezena_de_segundo_carry), .in1(m0b), .out(multiplexer_2_out), .sel(in_2));
  Multiplexer #(.enable("false")) multiplexer_3 (
    .in0(Unidade_de_segundo_carry), .in1(s1b), .out(multiplexer_3_out), .sel(in_2));
  Counter #(.width(4), .max('h5)) Dezena_de_segundo (
    .count(in_2), .Q(S1B_2), .carry(Dezena_de_segundo_carry), .clk(multiplexer_3_out));  // open: load, D, clr, preset, down
  Counter #(.width(4), .max('h9)) Unidade_de_segundo (
    .count(in_2), .Q(S0B_2), .carry(Unidade_de_segundo_carry), .clk(multiplexer_4_out));  // open: load, D, clr, preset, down
  Multiplexer #(.enable("false")) multiplexer_4 (.in0(and_1_out), .in1(s0b), .out(multiplexer_4_out), .sel(in_2));
  and and_1 (and_1_out, CLK, B_jogando);

  // Other names for the same wires on the sheet: B_jogando_t = in_1; Config = in_2

  // Notes on the sheet:
  //   Circuito de Cronômetro B
endmodule

module \Cronômetro_A  (
  input  Reset,
  input  Rodando,
  input  A_joganda,
  input  Config,
  input  m1a,
  input  m0a,
  input  s1a,
  input  s0a,
  input  CLK,
  output [3:0] M1A_2,
  output [3:0] M0A_2,
  output [3:0] S1A_2,
  output [3:0] S0A_2
);

  wire and_1_out, Cout0, Cout1, Cout2, multiplexer_1_out, multiplexer_2_out, multiplexer_3_out,
       multiplexer_4_out;

  Counter #(.width(4), .max('h5)) Dezena_de_minuto (
    .count(1'b1), .Q(M1A_2), .clk(multiplexer_1_out), .clr(Reset), .down(Rodando));  // open: load, D, carry, preset
  Multiplexer #(.enable("false")) multiplexer_1 (.in0(Cout2), .in1(m1a), .out(multiplexer_1_out), .sel(Config));
  Counter #(.width(4), .max('h9)) Unidade_de_minuto (
    .count(1'b1), .Q(M0A_2), .carry(Cout2), .clk(multiplexer_2_out), .clr(Reset), .down(Rodando));  // open: load, D, preset
  Multiplexer #(.enable("false")) multiplexer_2 (.in0(Cout1), .in1(m0a), .out(multiplexer_2_out), .sel(Config));
  Counter #(.width(4), .max('h5)) Dezena_de_segundo (
    .count(A_joganda), .Q(S1A_2), .carry(Cout1), .clk(multiplexer_3_out), .clr(Reset), .down(Rodando));  // open: load, D, preset
  Multiplexer #(.enable("false")) multiplexer_3 (.in0(Cout0), .in1(s1a), .out(multiplexer_3_out), .sel(Config));
  and and_1 (and_1_out, CLK, A_joganda);
  Counter #(.width(4), .max('h9)) Unidade_de_segundo (
    .count(A_joganda), .Q(S0A_2), .carry(Cout0), .clk(multiplexer_4_out), .clr(Reset), .down(Rodando));  // open: load, D, preset
  Multiplexer #(.enable("false")) multiplexer_4 (.in0(and_1_out), .in1(s0a), .out(multiplexer_4_out), .sel(Config));

  // Other names for the same wires on the sheet: A_jogando = A_joganda; Game_Reset = Reset

  // Notes on the sheet:
  //   Circuito de Cronômetro A
endmodule

module Palpite_A (
  input  Escolher_A,
  input  \Avançar ,
  input  Confirmar_A,
  output [3:0] \Número_X_escolhido ,
  output [3:0] \Número_Y_escolhido ,
  output [3:0] \Número_a_ser_escolhido ,
  output Fim_do_turno,
  output Escolhendo_Y,
  output Escolhendo_X
);

  wire demultiplexer_1_out0, demultiplexer_1_out1;

  Counter #(.width(4), .max('hf)) counter_1 (
    .Q(\Número_a_ser_escolhido ), .clk(Escolher_A), .clr(\Avançar ));  // open: load, D, count, carry, preset, down
  Register #(.width(4), .Select("low")) Number_X (
    .D(\Número_a_ser_escolhido ), .Q(\Número_X_escolhido ), .clk(demultiplexer_1_out0));  // open: en, clr
  Demultiplexer #(.enable("false")) demultiplexer_1 (
    .out0(demultiplexer_1_out0), .out1(demultiplexer_1_out1), .in(Confirmar_A), .sel(Escolhendo_Y));
  T_Flip_Flop #(.trigger("falling")) t_ff_1 (
    .clk(\Avançar ), .T(1'b1), .Q(Escolhendo_Y), .Qn(Escolhendo_X));  // open: preset, reset
  Register #(.width(4), .Select("low")) Number_Y (
    .D(\Número_a_ser_escolhido ), .Q(\Número_Y_escolhido ), .clk(demultiplexer_1_out1));  // open: en, clr
  and and_1 (Fim_do_turno, \Avançar , Escolhendo_Y);

  // Notes on the sheet:
  //   Circuito de Palpites A
endmodule

module Palpite_B (
  input  Escolher_B,
  input  \Avançar ,
  input  Confirmar_B,
  output [3:0] \Número_X_escolhido ,
  output [3:0] \Número_Y_escolhido ,
  output [3:0] \Número_a_ser_escolhido ,
  output Fim_do_turno,
  output Escolhendo_Y,
  output Escolhendo_X
);

  wire demultiplexer_1_out0, demultiplexer_1_out1;

  Counter #(.width(4), .max('hf)) counter_1 (
    .Q(\Número_a_ser_escolhido ), .clk(Escolher_B), .clr(\Avançar ));  // open: load, D, count, carry, preset, down
  Register #(.width(4), .Select("low")) Number_X (
    .D(\Número_a_ser_escolhido ), .Q(\Número_X_escolhido ), .clk(demultiplexer_1_out0));  // open: en, clr
  Demultiplexer #(.enable("false")) demultiplexer_1 (
    .out0(demultiplexer_1_out0), .out1(demultiplexer_1_out1), .in(Confirmar_B), .sel(Escolhendo_Y));
  T_Flip_Flop #(.trigger("falling")) t_ff_1 (
    .clk(\Avançar ), .T(1'b1), .Q(Escolhendo_Y), .Qn(Escolhendo_X));  // open: preset, reset
  Register #(.width(4), .Select("low")) Number_Y (
    .D(\Número_a_ser_escolhido ), .Q(\Número_Y_escolhido ), .clk(demultiplexer_1_out1));  // open: en, clr
  and and_1 (Fim_do_turno, \Avançar , Escolhendo_Y);

  // Notes on the sheet:
  //   Circuito de Palpites B
endmodule

module \Teste_Cronômetro_AB  (
);

  wire A_jogando, \Avançar_A , \Avançar_B , B_jogando, button_10_out, clk, Config, Confirmar_A, End_turno_A,
       Escolhendo_X, Escolhendo_Y, Escolher_A, Iniciar, m0a_t, m1a_t, Reset, Rodando, s0a_t, s1a_t,
       Soma_certa, undriven, X_certo, Y_certo;
  wire [3:0] gtn_x_1_x_r, gtn_x_1_y_r, M0A, M0B, M1A, M1B, S0A, S0B, S1A, S1B, V_A, X_Escolhido, Y_Escolhido;
  wire [7:0] B, R;

  Hex_Digit_Display hex_digit_display_1 (.value(M1A));  // open: dp
  Button button_1 (.out(m1a_t));
  Button button_2 (.out(Escolher_A));
  Hex_Digit_Display hex_digit_display_2 (.value(M0A));  // open: dp
  Button button_3 (.out(m0a_t));
  Hex_Digit_Display hex_digit_display_3 (.value(V_A));  // open: dp
  Button button_4 (.out(Confirmar_A));
  LED led_1 (.in(A_jogando));
  Controle_de_turnos controle_de_turnos_1 (
    .\Avançar_B (\Avançar_B ), .\Avançar_A (\Avançar_A ), .A_jogando(A_jogando), .B_jogando(B_jogando),
    .Iniciar_jogo(Iniciar), .Resetar_jogo(Reset));
  Hex_Digit_Display hex_digit_display_4 (.value(S0A));  // open: dp
  Hex_Digit_Display hex_digit_display_5 (.value(S1A));  // open: dp
  Button button_5 (.out(s1a_t));
  Button button_6 (.out(s0a_t));
  Button button_7 (.out(\Avançar_A ));
  cronometro_v3__Definitivo cronometro_v3_definitivo_1 (
    .A_joganda(A_jogando), .Reset(Reset), .Rodando(Rodando), .Config(Config), .CLK(clk), .M1A_2(M1A),
    .M0A_2(M0A), .S1A_2(S1A), .S0A_2(S0A), .m1a(m1a_t), .m0a(m0a_t), .s1a(s1a_t), .s0a(s0a_t));
  Estado_de_Jogo estado_de_jogo_1 (.Iniciar(Iniciar), .Game_Reset(Reset), .Rodando(Rodando), .End_Config(Config));
  Palpite_B palpite_b_1 ();  // open: Fim_do_turno, Escolhendo_Y, Escolhendo_X, Número_a_ser_escolhido, Número_X_escolhido, Número_Y_escolhido, Escolher_B, Confirmar_B, Avançar
  Clock clock_1 (.out(clk));
  LED led_2 (.in(X_certo));
  LED led_3 (.in(Soma_certa));
  Hex_Digit_Display hex_digit_display_6 (.value(X_Escolhido));  // open: dp
  LED led_4 (.in(Escolhendo_X));
  Button button_8 (.out(Iniciar));
  Palpite_A palpite_a_1 (
    .\Número_a_ser_escolhido (V_A), .\Número_X_escolhido (X_Escolhido), .\Número_Y_escolhido (Y_Escolhido),
    .Escolher_A(Escolher_A), .Confirmar_A(Confirmar_A), .\Avançar (\Avançar_A ), .Escolhendo_Y(Escolhendo_Y),
    .Escolhendo_X(Escolhendo_X), .Fim_do_turno(End_turno_A));
  // RGBLed #(.multibit("true")) rgbled_1: pin names not known; wires that end beside it: R, B, Escolher_A, Confirmar_A, Escolhendo_Y
  Hex_Digit_Display hex_digit_display_7 (.value(Y_Escolhido));  // open: dp
  LED led_5 (.in(Escolhendo_Y));
  Button button_9 (.out(Reset));
  LED led_6 (.in(Y_certo));
  cronometro_B_v3 cronometro_b_v3_1 (
    .B_joganda(B_jogando), .Reset(Reset), .Rodando(Rodando), .Config(Config), .CLK(clk), .M1B_2(M1B),
    .M0B_2(M0B), .S1B_2(S1B), .S0B_2(S0B), .m1b(m1a_t), .m0b(m0a_t), .s1b(s1a_t), .s0b(s0a_t));
  Button button_10 (.out(button_10_out));
  GTN_X gtn_x_1 (
    .Confirmar(undriven), .Novo(button_10_out), .X_CERTO(X_certo), .Y_CERTO(Y_certo),
    .SOMA_CERTA(Soma_certa), .X_R(gtn_x_1_x_r), .Y_R(gtn_x_1_y_r));  // open: x, y, VERMELHO, AZUL
  Hex_Digit_Display hex_digit_display_8 (.value(M0B));  // open: dp
  Hex_Digit_Display hex_digit_display_9 (.value(M1B));  // open: dp
  Button button_11 (.out(Escolher_A));
  Hex_Digit_Display hex_digit_display_10 (.value(gtn_x_1_x_r));  // open: dp
  Hex_Digit_Display hex_digit_display_11 (.value(S1B));  // open: dp
  Hex_Digit_Display hex_digit_display_12 (.value(V_A));  // open: dp
  Button button_12 (.out(Confirmar_A));
  LED led_7 (.in(B_jogando));
  Hex_Digit_Display hex_digit_display_13 (.value(gtn_x_1_y_r));  // open: dp
  Hex_Digit_Display hex_digit_display_14 (.value(S0B));  // open: dp
  Button button_13 (.out(\Avançar_B ));

  // Notes on the sheet:
  //   :
  //   :
endmodule

module cronometro_v1 (
  input  [3:0] s1a,
  input  [3:0] s0a,
  input  m1a,
  input  m0a,
  input  CLK,
  input  in_6,
  input  in_7,
  input  in_8,
  output [3:0] M1A_2,
  output [3:0] M0A_2,
  output [3:0] S1A_2,
  output [3:0] S0A_2
);

  wire and_1_out, and_2_out, and_3_out, Cout0, Cout1, Cout2, multiplexer_1_out, multiplexer_2_out;

  and and_1 (and_1_out, Cout2, and_2_out);
  Counter #(.width(4), .max('h5)) Dezena_de_minuto (
    .count(and_1_out), .Q(M1A_2), .clk(multiplexer_1_out), .down(in_6));  // open: load, D, carry, clr, preset
  Multiplexer #(.enable("false")) multiplexer_1 (.in0(CLK), .in1(m1a), .out(multiplexer_1_out), .sel(in_8));
  and and_2 (and_2_out, Cout1, and_3_out);
  Counter #(.width(4), .max('h9)) Unidade_de_minuto (
    .count(and_2_out), .Q(M0A_2), .carry(Cout2), .clk(multiplexer_2_out), .down(in_6));  // open: load, D, clr, preset
  Multiplexer #(.enable("false")) multiplexer_2 (.in0(CLK), .in1(m0a), .out(multiplexer_2_out), .sel(in_8));
  and and_3 (and_3_out, Cout0, in_7);
  Counter #(.width(4), .max('h5)) Dezena_de_segundo (
    .load(in_8), .D(s1a), .count(and_3_out), .Q(S1A_2), .carry(Cout1), .clk(CLK), .down(in_6));  // open: clr, preset
  Counter #(.width(4), .max('h9)) Unidade_de_segundo (
    .load(in_8), .D(s0a), .count(in_7), .Q(S0A_2), .carry(Cout0), .clk(CLK), .down(in_6));  // open: clr, preset

  // Other names for the same wires on the sheet: A_jogando = in_7; Config = in_8; Rodando = in_6

  // Notes on the sheet:
  //   Circuito de Cronômetro A
endmodule

module Cronometro_v2 (
  input  A_joganda,
  input  Reset,
  input  Rodando,
  input  Config,
  input  CLK,
  input  m1a,
  input  m0a,
  input  s1a,
  input  s0a,
  output [3:0] M1A_2,
  output [3:0] M0A_2,
  output [3:0] S1A_2,
  output [3:0] S0A_2
);

  wire and_1_out, and_2_out, and_3_out, and_4_out, and_5_out, and_6_out, and_7_out, Cout0, Cout1, Cout2,
       multiplexer_1_out, multiplexer_2_out, multiplexer_3_out, multiplexer_4_out, or_1_out, or_2_out,
       or_3_out, or_4_out, PM;

  or or_1 (or_1_out, Config, Rodando);
  Counter #(.width(4), .max('h5)) counter_1 (
    .count(or_1_out), .Q(M1A_2), .clk(multiplexer_1_out), .clr(Reset), .down(and_1_out));  // open: load, D, carry, preset
  and and_1 (and_1_out, A_joganda, Rodando);
  Multiplexer #(.enable("false")) multiplexer_1 (.in0(and_2_out), .in1(m1a), .out(multiplexer_1_out), .sel(Config));
  and and_2 (and_2_out, Cout2, PM, Cout0, Cout1);
  or or_2 (or_2_out, Config, Rodando);
  and and_3 (and_3_out, A_joganda, Rodando);
  Multiplexer #(.enable("false")) multiplexer_2 (.in0(and_4_out), .in1(m0a), .out(multiplexer_2_out), .sel(Config));
  and and_4 (and_4_out, Cout1, PM, Cout0);
  Counter #(.width(4), .max('h9)) counter_2 (
    .count(or_2_out), .Q(M0A_2), .carry(Cout2), .clk(multiplexer_2_out), .clr(Reset), .down(and_3_out));  // open: load, D, preset
  or or_3 (or_3_out, Config, Rodando);
  Counter #(.width(4), .max('h5)) counter_3 (
    .count(or_3_out), .Q(S1A_2), .carry(Cout1), .clk(multiplexer_3_out), .clr(Reset), .down(and_5_out));  // open: load, D, preset
  and and_5 (and_5_out, A_joganda, Rodando);
  Multiplexer #(.enable("false")) multiplexer_3 (.in0(and_6_out), .in1(s1a), .out(multiplexer_3_out), .sel(Config));
  and and_6 (and_6_out, Cout0, PM);
  and and_7 (and_7_out, A_joganda, Rodando);
  or or_4 (or_4_out, Config, Rodando);
  Counter #(.width(4), .max('h9)) counter_4 (
    .count(or_4_out), .Q(S0A_2), .carry(Cout0), .clk(multiplexer_4_out), .clr(Reset), .down(and_7_out));  // open: load, D, preset
  Multiplexer #(.enable("false")) multiplexer_4 (.in0(PM), .in1(s0a), .out(multiplexer_4_out), .sel(Config));
  and and_8 (PM, CLK, A_joganda);

  // Other names for the same wires on the sheet: A_jogando = A_joganda
endmodule

module cronometro_v3__Definitivo (
  input  A_joganda,
  input  Reset,
  input  Rodando,
  input  Config,
  input  CLK,
  input  m1a,
  input  m0a,
  input  s1a,
  input  s0a,
  output [3:0] M1A_2,
  output [3:0] M0A_2,
  output [3:0] S1A_2,
  output [3:0] S0A_2
);

  wire and_1_out, and_2_out, and_3_out, and_4_out, and_5_out, and_6_out, Cout0, Cout1, Cout2,
       multiplexer_1_out, multiplexer_2_out, multiplexer_3_out, multiplexer_4_out, or_1_out, or_2_out,
       or_3_out, or_4_out, PM;

  and and_1 (and_1_out, Cout1, Cout2, Cout0);
  or or_1 (or_1_out, Config, and_1_out);
  Counter #(.width(4), .max('h5)) counter_1 (
    .count(or_1_out), .Q(M1A_2), .clk(multiplexer_1_out), .clr(Reset), .down(and_2_out));  // open: load, D, carry, preset
  and and_2 (and_2_out, A_joganda, Rodando);
  Multiplexer #(.enable("false")) multiplexer_1 (.in0(PM), .in1(m1a), .out(multiplexer_1_out), .sel(Config));
  and and_3 (and_3_out, A_joganda, Rodando);
  and and_4 (and_4_out, Cout1, Cout0);
  or or_2 (or_2_out, Config, and_4_out);
  Counter #(.width(4), .max('h9)) counter_2 (
    .count(or_2_out), .Q(M0A_2), .carry(Cout2), .clk(multiplexer_2_out), .clr(Reset), .down(and_3_out));  // open: load, D, preset
  Multiplexer #(.enable("false")) multiplexer_2 (.in0(PM), .in1(m0a), .out(multiplexer_2_out), .sel(Config));
  or or_3 (or_3_out, Config, Cout0);
  Counter #(.width(4), .max('h5)) counter_3 (
    .count(or_3_out), .Q(S1A_2), .carry(Cout1), .clk(multiplexer_3_out), .clr(Reset), .down(and_5_out));  // open: load, D, preset
  and and_5 (and_5_out, A_joganda, Rodando);
  Multiplexer #(.enable("false")) multiplexer_3 (.in0(PM), .in1(s1a), .out(multiplexer_3_out), .sel(Config));
  or or_4 (or_4_out, Config, A_joganda);
  Counter #(.width(4), .max('h9)) counter_4 (
    .count(or_4_out), .Q(S0A_2), .carry(Cout0), .clk(multiplexer_4_out), .clr(Reset), .down(and_6_out));  // open: load, D, preset
  and and_6 (and_6_out, A_joganda, Rodando);
  Multiplexer #(.enable("false")) multiplexer_4 (.in0(PM), .in1(s0a), .out(multiplexer_4_out), .sel(Config));
  and and_7 (PM, CLK, A_joganda);

  // Other names for the same wires on the sheet: A_jogando = A_joganda
endmodule

module cronometro_B_v3 (
  input  B_joganda,
  input  Reset,
  input  Rodando,
  input  Config,
  input  CLK,
  input  m1b,
  input  m0b,
  input  s1b,
  input  s0b,
  output [3:0] M1B_2,
  output [3:0] M0B_2,
  output [3:0] S1B_2,
  output [3:0] S0B_2
);

  wire and_1_out, and_2_out, and_3_out, and_4_out, and_5_out, and_6_out, Cout0, Cout1, Cout2,
       multiplexer_1_out, multiplexer_2_out, multiplexer_3_out, multiplexer_4_out, or_1_out, or_2_out,
       or_3_out, or_4_out, PM;

  and and_1 (and_1_out, Cout1, Cout2, Cout0);
  or or_1 (or_1_out, Config, and_1_out);
  Counter #(.width(4), .max('h5)) counter_1 (
    .count(or_1_out), .Q(M1B_2), .clk(multiplexer_1_out), .clr(Reset), .down(and_2_out));  // open: load, D, carry, preset
  and and_2 (and_2_out, B_joganda, Rodando);
  Multiplexer #(.enable("false")) multiplexer_1 (.in0(PM), .in1(m1b), .out(multiplexer_1_out), .sel(Config));
  and and_3 (and_3_out, B_joganda, Rodando);
  and and_4 (and_4_out, Cout1, Cout0);
  or or_2 (or_2_out, Config, and_4_out);
  Counter #(.width(4), .max('h9)) counter_2 (
    .count(or_2_out), .Q(M0B_2), .carry(Cout2), .clk(multiplexer_2_out), .clr(Reset), .down(and_3_out));  // open: load, D, preset
  Multiplexer #(.enable("false")) multiplexer_2 (.in0(PM), .in1(m0b), .out(multiplexer_2_out), .sel(Config));
  or or_3 (or_3_out, Config, Cout0);
  Counter #(.width(4), .max('h5)) counter_3 (
    .count(or_3_out), .Q(S1B_2), .carry(Cout1), .clk(multiplexer_3_out), .clr(Reset), .down(and_5_out));  // open: load, D, preset
  and and_5 (and_5_out, B_joganda, Rodando);
  Multiplexer #(.enable("false")) multiplexer_3 (.in0(PM), .in1(s1b), .out(multiplexer_3_out), .sel(Config));
  or or_4 (or_4_out, Config, Rodando);
  Counter #(.width(4), .max('h9)) counter_4 (
    .count(or_4_out), .Q(S0B_2), .carry(Cout0), .clk(multiplexer_4_out), .clr(Reset), .down(and_6_out));  // open: load, D, preset
  and and_6 (and_6_out, B_joganda, Rodando);
  Multiplexer #(.enable("false")) multiplexer_4 (.in0(PM), .in1(s0b), .out(multiplexer_4_out), .sel(Config));
  and and_7 (PM, CLK, B_joganda);

  // Other names for the same wires on the sheet: B_jogando = B_joganda
endmodule
