// Logisim project Projeto Ramon_Copia.circ as structural Verilog: 10 circuits, main circuit main
module main (
  input  [3:0] Entrada
);

  wire decoder_1_s, decoder_1_u, decoder_1_v, decoder_1_w, decoder_1_x, decoder_1_y, decoder_1_z;

  Decoder decoder_1 (
    .a(Entrada[3]), .b(Entrada[2]), .c(Entrada[1]), .d(Entrada[0]), .x(decoder_1_x), .y(decoder_1_y),
    .z(decoder_1_z), .u(decoder_1_u), .v(decoder_1_v), .w(decoder_1_w), .s(decoder_1_s));
  _7_Segment_Display u_7_segment_display_1 (
    .g(decoder_1_s), .f(decoder_1_w), .a(decoder_1_x), .b(decoder_1_y), .e(decoder_1_v), .d(decoder_1_u),
    .c(decoder_1_z));  // open: dp
endmodule

// DECODER
module Decoder (
  input  a,
  input  b,
  input  c,
  input  d,
  output x,
  output y,
  output z,
  output u,
  output v,
  output w,
  output s
);

  wire and_1_out, and_2_out, and_3_out, and_4_out, and_5_out, and_6_out, and_7_out, and_8_out, and_9_out,
       and_10_out, and_11_out, and_12_out, and_13_out, and_14_out, and_15_out, and_16_out, and_17_out,
       and_18_out, and_19_out, and_20_out, and_21_out, and_22_out, and_23_out, and_24_out, and_25_out,
       and_26_out, and_27_out, and_28_out, and_29_out, and_30_out, and_31_out, and_32_out, not_1_out,
       not_2_out, not_3_out, not_4_out, not_5_out, not_6_out, not_7_out, not_8_out, not_9_out, not_10_out,
       not_11_out, not_12_out, not_13_out, not_14_out, not_15_out, not_16_out, not_17_out, not_18_out,
       not_19_out, not_20_out, not_21_out, not_22_out, not_23_out, not_24_out, not_25_out, not_26_out,
       not_27_out, not_28_out, not_29_out, not_30_out, not_31_out, not_32_out, not_33_out, not_34_out,
       not_35_out, not_36_out, not_37_out, not_38_out, not_39_out, not_40_out, not_41_out;

  not not_1 (not_1_out, a);
  and and_1 (and_1_out, not_1_out, not_2_out, not_3_out);
  not not_2 (not_2_out, b);
  not not_3 (not_3_out, d);
  not not_4 (not_4_out, a);
  and and_2 (and_2_out, not_4_out, c);
  not not_5 (not_5_out, a);
  and and_3 (and_3_out, not_5_out, b, d);
  and and_4 (and_4_out, b, c);
  not not_6 (not_6_out, b);
  and and_5 (and_5_out, a, not_6_out, not_7_out);
  not not_7 (not_7_out, c);
  not not_8 (not_8_out, a);
  and and_6 (and_6_out, not_8_out, not_9_out);
  not not_9 (not_9_out, b);
  not not_10 (not_10_out, a);
  and and_7 (and_7_out, not_10_out, not_11_out, not_12_out);
  not not_11 (not_11_out, c);
  not not_12 (not_12_out, d);
  not not_13 (not_13_out, b);
  and and_8 (and_8_out, not_13_out, not_14_out);
  not not_14 (not_14_out, c);
  not not_15 (not_15_out, a);
  and and_9 (and_9_out, not_15_out, c, d);
  not not_16 (not_16_out, c);
  and and_10 (and_10_out, a, not_16_out, d);
  not not_17 (not_17_out, a);
  and and_11 (and_11_out, not_17_out, not_18_out);
  not not_18 (not_18_out, c);
  not not_19 (not_19_out, a);
  and and_12 (and_12_out, not_19_out, d);
  not not_20 (not_20_out, c);
  and and_13 (and_13_out, not_20_out, d);
  not not_21 (not_21_out, a);
  and and_14 (and_14_out, not_21_out, b);
  and and_15 (and_15_out, a, not_22_out);
  not not_22 (not_22_out, b);
  not not_23 (not_23_out, b);
  and and_16 (and_16_out, not_23_out, not_24_out);
  not not_24 (not_24_out, d);
  not not_25 (not_25_out, b);
  and and_17 (and_17_out, not_25_out, c);
  and and_18 (and_18_out, c, not_26_out);
  not not_26 (not_26_out, d);
  not not_27 (not_27_out, c);
  and and_19 (and_19_out, b, not_27_out, d);
  and and_20 (and_20_out, a, not_28_out);
  not not_28 (not_28_out, c);
  not not_29 (not_29_out, b);
  and and_21 (and_21_out, not_29_out, not_30_out);
  not not_30 (not_30_out, d);
  and and_22 (and_22_out, c, not_31_out);
  not not_31 (not_31_out, d);
  and and_23 (and_23_out, a, c);
  and and_24 (and_24_out, a, b);
  not not_32 (not_32_out, b);
  not not_33 (not_33_out, c);
  and and_25 (and_25_out, not_32_out, not_33_out, not_34_out);
  not not_34 (not_34_out, d);
  not not_35 (not_35_out, a);
  and and_26 (and_26_out, not_35_out, b, not_36_out);
  not not_36 (not_36_out, c);
  and and_27 (and_27_out, b, c, not_37_out);
  not not_37 (not_37_out, d);
  and and_28 (and_28_out, a, not_38_out, d);
  not not_38 (not_38_out, b);
  and and_29 (and_29_out, a, b, c);
  not not_39 (not_39_out, b);
  and and_30 (and_30_out, not_39_out, c);
  and and_31 (and_31_out, b, not_40_out);
  not not_40 (not_40_out, c);
  and and_32 (and_32_out, b, not_41_out);
  not not_41 (not_41_out, d);
  or or_1 (x, and_1_out, and_2_out, and_3_out, and_4_out, and_5_out);
  or or_2 (y, and_6_out, and_7_out, and_8_out, and_9_out, and_10_out);
  or or_3 (z, and_11_out, and_12_out, and_13_out, and_14_out, and_15_out);
  or or_4 (u, and_16_out, and_17_out, and_18_out, and_19_out, and_20_out);
  or or_5 (v, and_21_out, and_22_out, and_23_out, and_24_out);
  or or_6 (w, and_25_out, and_26_out, and_27_out, and_28_out, and_29_out);
  or or_7 (s, and_30_out, and_31_out, and_32_out, a);
endmodule

// SUBTRATOR
module Subtrator (
  input  [3:0] in_1,
  input  [3:0] in_2,
  output [3:0] out_3
);

  wire sub1_out_5, sub2_out_5, sub3_out_5;

  \SUBTRAÇAO  sub1 (.a(in_1[0]), .b(in_2[0]), .BIN(1'b0), .out_4(out_3[0]), .out_5(sub1_out_5));
  \SUBTRAÇAO  sub2 (.a(in_1[1]), .b(in_2[1]), .BIN(sub1_out_5), .out_4(out_3[1]), .out_5(sub2_out_5));
  \SUBTRAÇAO  sub3 (.a(in_1[2]), .b(in_2[2]), .BIN(sub2_out_5), .out_4(out_3[2]), .out_5(sub3_out_5));
  \SUBTRAÇAO  sub4 (.a(in_1[3]), .b(in_2[3]), .BIN(sub3_out_5), .out_4(out_3[3]));  // open: out_5
endmodule

module \SUBTRAÇAO  (
  input  a,
  input  b,
  input  BIN,
  output out_4,
  output out_5
);

  wire and_1_out, and_2_out, and_3_out, xor_1_out;

  and and_1 (and_1_out, ~a, b);  // AND_Gate
  and and_2 (and_2_out, ~a, BIN);  // AND_Gate
  and and_3 (and_3_out, b, BIN);
  or BOUT (out_5, and_1_out, and_2_out, and_3_out);
  xor xor_1 (xor_1_out, a, b);
  xor diff (out_4, xor_1_out, BIN);
endmodule

module Multiplex1bit (
  input  I0,
  input  I1,
  input  S,
  output out_4
);

  wire and_1_out, and_2_out, not_1_out;

  not not_1 (not_1_out, S);
  and and_1 (and_1_out, I0, not_1_out);
  and and_2 (and_2_out, I1, S);
  or or_1 (out_4, and_1_out, and_2_out);
endmodule

module Multiplex4bits (
  input  [3:0] A,
  input  [3:0] B,
  input  S,
  output [3:0] \Saída 
);

  Multiplex1bit multiplex1bit_1 (.I0(A[0]), .I1(B[0]), .S(S), .out_4(\Saída [0]));
  Multiplex1bit multiplex1bit_2 (.I0(A[1]), .I1(B[1]), .S(S), .out_4(\Saída [1]));
  Multiplex1bit multiplex1bit_3 (.I0(A[2]), .I1(B[2]), .S(S), .out_4(\Saída [2]));
  Multiplex1bit multiplex1bit_4 (.I0(A[3]), .I1(B[3]), .S(S), .out_4(\Saída [3]));
endmodule

module Subtrator_completo (
  input  [3:0] Sorteador,
  input  [3:0] Chute,
  output [3:0] \Diferença 
);

  wire main_1_p2;
  wire [3:0] \multiplex4bits_1_saída , \multiplex4bits_2_saída ;

  // Comparador_main main_1: pin names not known; wires that end beside it: Chute, main_1_p2, Sorteador, Sorteador, Chute
  Multiplex4bits multiplex4bits_1 (.A(Chute), .B(Sorteador), .\Saída (\multiplex4bits_1_saída ), .S(main_1_p2));
  Subtrator subtrator_1 (.out_3(\Diferença ), .in_1(\multiplex4bits_1_saída ), .in_2(\multiplex4bits_2_saída ));
  Multiplex4bits multiplex4bits_2 (.A(Sorteador), .B(Chute), .\Saída (\multiplex4bits_2_saída ), .S(main_1_p2));
endmodule

module cores (
  input  [3:0] \Diferença ,
  output [7:0] Vermelho,
  output [7:0] Azul
);

  wire button_1_out;
  wire [3:0] main_1_p2;

  Button button_1 (.out(button_1_out));
  Hex_Digit_Display hex_digit_display_1 (.value(main_1_p2));  // open: dp
  // Sorteador_main main_1: pin names not known; wires that end beside it: button_1_out, main_1_p2
  assign Vermelho[7:4] = ~Azul[7:4];  // NOT_Gate not_1, 4 bits wide
  Subtrator_completo subtrator_completo_1 (.Sorteador(main_1_p2), .Chute(\Diferença ), .\Diferença (Azul[7:4]));
  // RGBLed #(.multibit("true")) rgbled_1: pin names not known; wires that end beside it: {8{1'b0}}

  assign Azul[3:0] = Azul[7:4];
  assign Vermelho[3:0] = Vermelho[7:4];
endmodule

module teste (
  input  Confirmar,
  input  Sortear,
  input  [3:0] Chute,
  output [7:0] Vermelho,
  output [7:0] Azul,
  output Acertou
);

  wire main_2_p3;
  wire [3:0] main_1_p2, \subtrator_completo_1_diferença ;
  wire [7:0] cores_1_azul, cores_1_vermelho;

  // Sorteador_main main_1: pin names not known; wires that end beside it: Sortear, main_1_p2
  Subtrator_completo subtrator_completo_1 (
    .Sorteador(main_1_p2), .Chute(Chute), .\Diferença (\subtrator_completo_1_diferença ));
  // Comparador_main main_2: pin names not known; wires that end beside it: main_1_p2, Chute, main_2_p3
  cores cores_1 (.\Diferença (\subtrator_completo_1_diferença ), .Vermelho(cores_1_vermelho), .Azul(cores_1_azul));
  Register #(.Select("low")) register_1 (
    .D(cores_1_vermelho), .Q(Vermelho), .clk(Confirmar), .clr(Sortear));  // open: en
  Register #(.Select("low")) register_2 (.D(cores_1_azul), .Q(Azul), .clk(Confirmar), .clr(Sortear));  // open: en
  D_Flip_Flop d_ff_1 (.clk(Confirmar), .D(main_2_p3), .Q(Acertou), .reset(Sortear));  // open: Qn, preset

  // Notes on the sheet:
  //   Sorteador
  //   Diferença
  //   Comparador
  //   Cores
endmodule

module teste_main (
  input  [3:0] in_1
);

  wire button_1_out, button_2_out, teste_1_acertou;
  wire [7:0] rgbled_1_p1, rgbled_1_p2;

  Button button_1 (.out(button_1_out));
  // RGBLed #(.multibit("true")) rgbled_1: pin names not known; wires that end beside it: rgbled_1_p1, rgbled_1_p2
  teste teste_1 (
    .Sortear(button_1_out), .Acertou(teste_1_acertou), .Confirmar(button_2_out), .Chute(in_1),
    .Azul(rgbled_1_p2), .Vermelho(rgbled_1_p1));
  Button button_2 (.out(button_2_out));
  LED led_1 (.in(teste_1_acertou));

  // Notes on the sheet:
  //   Sortear
  //   Termômetro
  //   Confimar
  //   Acertou
endmodule
